// Logisim project relogio.circ as structural Verilog: 8 circuits, main circuit main
module main (
  input  in_1
);

  wire clock_1_out, contador_completo_1_out_4, contador_completo_1_out_5, contador_completo_1_out_6,
       contador_completo_1_out_7, contador_completo_1_out_8, contador_completo_1_out_9,
       contador_completo_1_out_10, contador_completo_1_out_11, contador_completo_1_out_12,
       contador_completo_1_out_13, contador_completo_1_out_14, contador_completo_1_out_15,
       contador_completo_1_out_16, contador_completo_1_out_17, contador_completo_1_out_18,
       contador_completo_1_out_19, contador_completo_1_out_20, contador_completo_1_out_21,
       contador_completo_1_out_22, contador_completo_1_out_23, contador_completo_1_out_24,
       contador_completo_1_out_25, contador_completo_1_out_26, contador_completo_1_out_27,
       decodificador4bin_0_9dec_1_a, decodificador4bin_0_9dec_1_b, decodificador4bin_0_9dec_1_c,
       decodificador4bin_0_9dec_1_d, decodificador4bin_0_9dec_1_e, decodificador4bin_0_9dec_1_f,
       decodificador4bin_0_9dec_1_out_11;

  decodificador4bin_0_9dec decodificador4bin_0_9dec_1 (
    .in_1(contador_completo_1_out_5), .in_2(contador_completo_1_out_6), .in_3(contador_completo_1_out_7),
    .in_4(contador_completo_1_out_8), .a(decodificador4bin_0_9dec_1_a), .b(decodificador4bin_0_9dec_1_b),
    .c(decodificador4bin_0_9dec_1_c), .d(decodificador4bin_0_9dec_1_d), .e(decodificador4bin_0_9dec_1_e),
    .f(decodificador4bin_0_9dec_1_f), .out_11(decodificador4bin_0_9dec_1_out_11));
  _7_Segment_Display u_7_segment_display_1 (
    .g(decodificador4bin_0_9dec_1_out_11), .f(decodificador4bin_0_9dec_1_f),
    .a(decodificador4bin_0_9dec_1_a), .b(decodificador4bin_0_9dec_1_b), .e(decodificador4bin_0_9dec_1_e),
    .d(decodificador4bin_0_9dec_1_d), .c(decodificador4bin_0_9dec_1_c));  // open: dp
  Clock clock_1 (.out(clock_1_out));
  decodificador4bin_0_9dec decodificador4bin_0_9dec_2 (
    .in_1(contador_completo_1_out_9), .in_2(contador_completo_1_out_10), .in_3(contador_completo_1_out_11),
    .in_4(contador_completo_1_out_12));  // open: a, b, c, d, e, f, out_11
  contador_completo contador_completo_1 (
    .PRESET(in_1), .clock(clock_1_out), .VCC(1'b1), .out_5(contador_completo_1_out_5),
    .out_6(contador_completo_1_out_6), .out_7(contador_completo_1_out_7), .out_8(contador_completo_1_out_8),
    .out_9(contador_completo_1_out_9), .out_10(contador_completo_1_out_10),
    .out_11(contador_completo_1_out_11), .out_12(contador_completo_1_out_12),
    .out_13(contador_completo_1_out_13), .out_14(contador_completo_1_out_14),
    .out_15(contador_completo_1_out_15), .out_16(contador_completo_1_out_16),
    .out_17(contador_completo_1_out_17), .out_18(contador_completo_1_out_18),
    .out_19(contador_completo_1_out_19), .out_20(contador_completo_1_out_20),
    .out_21(contador_completo_1_out_21), .out_4(contador_completo_1_out_4),
    .out_22(contador_completo_1_out_22), .out_23(contador_completo_1_out_23),
    .out_24(contador_completo_1_out_24), .out_25(contador_completo_1_out_25),
    .out_26(contador_completo_1_out_26), .out_27(contador_completo_1_out_27));
  decodificador4bin_0_9dec decodificador4bin_0_9dec_3 (
    .in_1(contador_completo_1_out_13), .in_2(contador_completo_1_out_14), .in_3(contador_completo_1_out_15),
    .in_4(contador_completo_1_out_16));  // open: a, b, c, d, e, f, out_11
  decodificador4bin_0_9dec decodificador4bin_0_9dec_4 (
    .in_1(contador_completo_1_out_17), .in_2(contador_completo_1_out_18), .in_3(contador_completo_1_out_19),
    .in_4(contador_completo_1_out_20));  // open: a, b, c, d, e, f, out_11
  decodificador4bin_0_9dec decodificador4bin_0_9dec_5 (
    .in_1(contador_completo_1_out_21), .in_2(contador_completo_1_out_4), .in_3(contador_completo_1_out_22),
    .in_4(contador_completo_1_out_23));  // open: a, b, c, d, e, f, out_11
  decodificador4bin_0_9dec decodificador4bin_0_9dec_6 (
    .in_1(contador_completo_1_out_24), .in_2(contador_completo_1_out_25), .in_3(contador_completo_1_out_26),
    .in_4(contador_completo_1_out_27));  // open: a, b, c, d, e, f, out_11
endmodule

module contador4bits (
  input  PRESET,
  input  CLK,
  input  VCC,
  output out_4,
  output out_5,
  output out_6,
  output out_7,
  output out_8
);

  wire fliflopjk_1_out_7, fliflopjk_2_out_7, fliflopjk_3_out_7;

  and and_1 (out_8, out_7, fliflopjk_3_out_7, out_5, fliflopjk_1_out_7);
  fliflopjk fliflopjk_1 (
    .PRESET(PRESET), .J(VCC), .CLK(CLK), .K(VCC), .CLEAR(out_8), .out_6(out_4), .out_7(fliflopjk_1_out_7));
  fliflopjk fliflopjk_2 (
    .PRESET(PRESET), .J(VCC), .CLK(fliflopjk_1_out_7), .K(VCC), .CLEAR(out_8), .out_6(out_5),
    .out_7(fliflopjk_2_out_7));
  fliflopjk fliflopjk_3 (
    .PRESET(PRESET), .J(VCC), .CLK(fliflopjk_2_out_7), .K(VCC), .CLEAR(out_8), .out_6(out_6),
    .out_7(fliflopjk_3_out_7));
  fliflopjk fliflopjk_4 (
    .PRESET(PRESET), .J(VCC), .CLK(fliflopjk_3_out_7), .K(VCC), .CLEAR(out_8), .out_6(out_7));  // open: out_7

  // Notes on the sheet:
  //   VCC: pull=up
  //   CLK: pull=up
  //   out_6: pull=up
  //   out_7: pull=up
  //   out_4: pull=up
  //   PRESET: pull=up
  //   out_8: pull=up
  //   out_5: pull=up
endmodule

module fliflopjk (
  input  PRESET,
  input  J,
  input  CLK,
  input  K,
  input  CLEAR,
  output out_6,
  output out_7
);

  wire nand_1_out, nand_2_out, nand_3_out, nand_4_out, nand_5_out, nand_6_out, not_1_out, not_2_out,
       not_3_out, or_1_out;

  not not_1 (not_1_out, or_1_out);
  or or_1 (or_1_out, PRESET, CLEAR);
  not not_2 (not_2_out, CLK);
  nand nand_1 (nand_1_out, out_7, J, not_2_out);
  nand nand_2 (nand_2_out, not_2_out, K, out_6);
  nand nand_3 (nand_3_out, 1'b1, nand_1_out, nand_4_out);
  nand nand_4 (nand_4_out, nand_3_out, nand_2_out, not_1_out);
  nand nand_5 (nand_5_out, not_1_out, nand_3_out, not_3_out);
  not not_3 (not_3_out, not_2_out);
  nand nand_6 (nand_6_out, not_3_out, nand_4_out, 1'b1);
  nand nand_7 (out_6, 1'b1, nand_5_out, out_7);
  nand nand_8 (out_7, out_6, nand_6_out, not_1_out);

  // Notes on the sheet:
  //   out_6: pull=up
  //   CLK: pull=up
  //   J: pull=up
  //   out_7: pull=up
  //   K: pull=up
  //   CLEAR: pull=up
endmodule

module contador_completo (
  input  PRESET,
  input  clock,
  input  VCC,
  output out_4,
  output out_5,
  output out_6,
  output out_7,
  output out_8,
  output out_9,
  output out_10,
  output out_11,
  output out_12,
  output out_13,
  output out_14,
  output out_15,
  output out_16,
  output out_17,
  output out_18,
  output out_19,
  output out_20,
  output out_21,
  output out_22,
  output out_23,
  output out_24,
  output out_25,
  output out_26,
  output out_27
);

  wire contador4bits6_1_out_8, contador4bits6_2_out_8, contador4bits_1_out_8, contador4bits_2_out_8,
       counthourdec_1_soutforcount, hourcont_1_sout;

  contador4bits contador4bits_1 (
    .out_8(contador4bits_1_out_8), .out_4(out_5), .out_5(out_6), .out_6(out_7), .out_7(out_8),
    .PRESET(PRESET), .VCC(VCC), .CLK(clock));
  contador4bits6 contador4bits6_1 (
    .PRESET(PRESET), .CLK(contador4bits_1_out_8), .VCC(VCC), .out_4(out_9), .out_5(out_10), .out_6(out_11),
    .out_7(out_12), .out_8(contador4bits6_1_out_8));
  contador4bits contador4bits_2 (
    .out_8(contador4bits_2_out_8), .out_4(out_13), .out_5(out_14), .out_6(out_15), .out_7(out_16),
    .PRESET(PRESET), .VCC(VCC), .CLK(contador4bits6_1_out_8));
  contador4bits6 contador4bits6_2 (
    .PRESET(PRESET), .CLK(contador4bits_2_out_8), .VCC(VCC), .out_4(out_17), .out_5(out_18), .out_6(out_19),
    .out_7(out_20), .out_8(contador4bits6_2_out_8));
  hourCont hourcont_1 (
    .PRESET(PRESET), .CLK(contador4bits6_2_out_8), .VCC(VCC), .Sin(counthourdec_1_soutforcount), .q1(out_21),
    .q2(out_4), .q3(out_22), .q4(out_23), .Sout(hourcont_1_sout));
  countHourDec counthourdec_1 (
    .PRESET(PRESET), .CLK(hourcont_1_sout), .VCC(VCC), .q1(out_24), .q2(out_25), .q3(out_26), .q4(out_27),
    .soutForCount(counthourdec_1_soutforcount));

  // Notes on the sheet:
  //   out_11: pull=up
  //   out_13: pull=up
  //   out_27: pull=up
  //   out_5: pull=up
  //   out_9: pull=up
  //   out_24: pull=up
  //   out_23: pull=up
  //   out_18: pull=up
  //   out_20: pull=up
  //   VCC: pull=up
  //   out_19: pull=up
  //   out_12: pull=up
  //   PRESET: pull=up
  //   out_16: pull=up
  //   out_8: pull=up
  //   out_22: pull=up
  //   out_15: pull=up
  //   out_7: pull=up
  //   out_4: pull=up
  //   out_10: pull=up
  //   out_21: pull=up
  //   out_17: pull=up
  //   out_14: pull=up
  //   out_25: pull=up
  //   out_26: pull=up
  //   out_6: pull=up
endmodule

module decodificador4bin_0_9dec (
  input  in_1,
  input  in_2,
  input  in_3,
  input  in_4,
  output a,
  output b,
  output c,
  output d,
  output e,
  output f,
  output out_11
);

  wire and_1_out, and_2_out, and_3_out, and_4_out, and_5_out, and_6_out, not_1_out, not_2_out, not_3_out,
       not_4_out;

  not not_1 (not_1_out, in_1);
  not not_2 (not_2_out, in_2);
  not not_3 (not_3_out, in_3);
  not not_4 (not_4_out, in_4);
  and and_1 (and_1_out, not_1_out, not_2_out, not_3_out);
  and and_2 (and_2_out, not_1_out, in_2, not_4_out);
  or or_1 (a, and_1_out, and_2_out, and_3_out);
  and and_3 (and_3_out, in_1, not_3_out, not_4_out);
  and and_4 (and_4_out, not_1_out, not_2_out, not_4_out);
  and and_5 (and_5_out, in_1, not_3_out, in_4);
  or or_2 (b, and_1_out, and_4_out, and_5_out);
  or or_3 (c, and_1_out, and_4_out, and_5_out);
  or or_4 (d, and_1_out, and_4_out, and_5_out);
  or or_5 (e, and_1_out, and_4_out, and_6_out);
  and and_6 (and_6_out, in_1, not_3_out, not_4_out);
  or or_6 (f, and_1_out, and_4_out, and_5_out);
  or or_7 (out_11, and_1_out, and_6_out);

  // Notes on the sheet:
  //   c: pull=up
  //   b: pull=up
  //   a: pull=up
  //   in_4: pull=up
  //   f: pull=up
  //   in_3: pull=up
  //   out_11: pull=up
  //   e: pull=up
  //   in_2: pull=up
  //   in_1: pull=up
  //   d: pull=up
endmodule

module contador4bits6 (
  input  PRESET,
  input  CLK,
  input  VCC,
  output out_4,
  output out_5,
  output out_6,
  output out_7,
  output out_8
);

  wire fliflopjk_1_out_7, fliflopjk_2_out_7, fliflopjk_3_out_7, fliflopjk_4_out_7;

  and and_1 (out_8, fliflopjk_4_out_7, out_5, out_6, fliflopjk_1_out_7);
  fliflopjk fliflopjk_1 (
    .PRESET(PRESET), .J(VCC), .CLK(CLK), .K(VCC), .CLEAR(out_8), .out_6(out_4), .out_7(fliflopjk_1_out_7));
  fliflopjk fliflopjk_2 (
    .PRESET(PRESET), .J(VCC), .CLK(fliflopjk_1_out_7), .K(VCC), .CLEAR(out_8), .out_6(out_5),
    .out_7(fliflopjk_2_out_7));
  fliflopjk fliflopjk_3 (
    .PRESET(PRESET), .J(VCC), .CLK(fliflopjk_2_out_7), .K(VCC), .CLEAR(out_8), .out_6(out_6),
    .out_7(fliflopjk_3_out_7));
  fliflopjk fliflopjk_4 (
    .PRESET(PRESET), .J(VCC), .CLK(fliflopjk_3_out_7), .K(VCC), .CLEAR(out_8), .out_6(out_7),
    .out_7(fliflopjk_4_out_7));

  // Notes on the sheet:
  //   out_7: pull=up
  //   out_4: pull=up
  //   out_6: pull=up
  //   CLK: pull=up
  //   out_8: pull=up
  //   PRESET: pull=up
  //   VCC: pull=up
  //   out_5: pull=up
endmodule

module hourCont (
  input  PRESET,
  input  CLK,
  input  VCC,
  input  Sin,
  output q1,
  output q2,
  output q3,
  output q4,
  output Sout
);

  wire and_1_out, and_2_out, fliflopjk_1_out_7, fliflopjk_2_out_7, fliflopjk_3_out_7, fliflopjk_4_out_7;

  and and_1 (and_1_out, q4, fliflopjk_3_out_7, q2, fliflopjk_1_out_7);
  fliflopjk fliflopjk_1 (
    .PRESET(PRESET), .J(VCC), .CLK(CLK), .K(VCC), .CLEAR(Sout), .out_6(q1), .out_7(fliflopjk_1_out_7));
  and and_2 (and_2_out, Sin, q2, q1, q2, fliflopjk_4_out_7);
  fliflopjk fliflopjk_2 (
    .PRESET(PRESET), .J(VCC), .CLK(fliflopjk_1_out_7), .K(VCC), .CLEAR(Sout), .out_6(q2),
    .out_7(fliflopjk_2_out_7));
  fliflopjk fliflopjk_3 (
    .PRESET(PRESET), .J(VCC), .CLK(fliflopjk_2_out_7), .K(VCC), .CLEAR(Sout), .out_6(q3),
    .out_7(fliflopjk_3_out_7));
  or or_1 (Sout, and_1_out, and_2_out);
  fliflopjk fliflopjk_4 (
    .PRESET(PRESET), .J(VCC), .CLK(fliflopjk_3_out_7), .K(VCC), .CLEAR(Sout), .out_6(q4),
    .out_7(fliflopjk_4_out_7));

  // Notes on the sheet:
  //   VCC: pull=up
  //   PRESET: pull=up
  //   q2: pull=up
  //   q1: pull=up
  //   q4: pull=up
  //   Sout: pull=up
  //   q3: pull=up
  //   CLK: pull=up
endmodule

module countHourDec (
  input  PRESET,
  input  CLK,
  input  VCC,
  output q1,
  output q2,
  output q3,
  output q4,
  output soutForCount
);

  wire and_1_out, fliflopjk_1_out_7, fliflopjk_2_out_7, fliflopjk_3_out_7, fliflopjk_4_out_7;

  and and_1 (and_1_out, fliflopjk_1_out_7, q2, fliflopjk_4_out_7, fliflopjk_3_out_7);
  and and_2 (soutForCount, q1, fliflopjk_2_out_7, fliflopjk_3_out_7, fliflopjk_4_out_7);
  fliflopjk fliflopjk_1 (
    .PRESET(PRESET), .J(VCC), .CLK(CLK), .K(VCC), .CLEAR(and_1_out), .out_6(q1), .out_7(fliflopjk_1_out_7));
  fliflopjk fliflopjk_2 (
    .PRESET(PRESET), .J(VCC), .CLK(fliflopjk_1_out_7), .K(VCC), .CLEAR(and_1_out), .out_6(q2),
    .out_7(fliflopjk_2_out_7));
  fliflopjk fliflopjk_3 (
    .PRESET(PRESET), .J(VCC), .CLK(fliflopjk_2_out_7), .K(VCC), .CLEAR(and_1_out), .out_6(q3),
    .out_7(fliflopjk_3_out_7));
  fliflopjk fliflopjk_4 (
    .PRESET(PRESET), .J(VCC), .CLK(fliflopjk_3_out_7), .K(VCC), .CLEAR(and_1_out), .out_6(q4),
    .out_7(fliflopjk_4_out_7));

  // Notes on the sheet:
  //   q1: pull=up
  //   VCC: pull=up
  //   q3: pull=up
  //   CLK: pull=up
  //   q2: pull=up
  //   q4: pull=up
  //   PRESET: pull=up
  //   soutForCount: pull=up
endmodule
